// Logisim project trabalho_2_pipeline.circ as structural Verilog: 10 circuits, main circuit PC_e_MI
module trabalho (
  output [7:0] out_1
);

  wire ALUSrc, ALUSrc_2, and_1_out, Branch, Branch_2, clk, Incr, Incr_2, MemtoReg, not_1_out, not_2_out,
       not_3_out, PCSrc, PCSumSrc, RegWr, Reset_out, salto, Zero;
  wire [1:0] pipeline1_1_out_9, ra_2, rd, rd_2, rd_3, rd_4;
  wire [3:0] ALUOp, ALUOp_2, opcode, opcode_2, opcode_3, opcode_4, pipeline1_1_out_11;
  wire [7:0] adder_1_out, adder_2_out, banco_de_registradores_1_saida_1, banco_de_registradores_1_saida_2,
       data, data_2, Imm, Imm_2, multiplexer_1_out, multiplexer_2_out, multiplexer_4_out, multiplexer_5_out,
       PC_2, PC_3, PC_4, pc_e_mi_1_instr, ra, ra_3, rb, rb_2, rb_3, rULA, rULA_2, TA, ula_1_out_7;

  Adder adder_1 (.a(out_1), .b(8'h1), .out(adder_1_out), .cin(1'b0));  // open: cout
  or or_1 (PCSrc, and_1_out, salto);
  Multiplexer #(.width(8)) multiplexer_1 (.in0(adder_1_out), .in1(TA), .out(multiplexer_1_out), .sel(PCSrc));
  and and_1 (and_1_out, pc_e_mi_1_instr[4], not_1_out, not_2_out, not_3_out);
  Clock clock_1 (.out(clk));
  not not_1 (not_1_out, pc_e_mi_1_instr[5]);
  not not_2 (not_2_out, pc_e_mi_1_instr[6]);
  not not_3 (not_3_out, pc_e_mi_1_instr[7]);
  PC_e_MI pc_e_mi_1 (
    .clk(clk), .PC(multiplexer_1_out), .addr(rb_2), .d(ra_3), .out_7(out_1), .instr(pc_e_mi_1_instr),
    .data(data));
  pipeline1 pipeline1_1 (
    .clk(clk), .reset(PCSrc), .rb(pc_e_mi_1_instr[1:0]), .ra(pc_e_mi_1_instr[3:2]),
    .imm(pc_e_mi_1_instr[3:0]), .opcode(pc_e_mi_1_instr[7:4]), .PC(out_1), .out_9(pipeline1_1_out_9),
    .out_10(ra_2), .out_11(pipeline1_1_out_11), .out_12(opcode), .out_8(PC_2));
  Button Reset (.out(Reset_out));
  assign Imm = {{4{pipeline1_1_out_11[3]}}, pipeline1_1_out_11};  // Bit_Extender bit_extender_1
  Multiplexer #(.width(8)) multiplexer_2 (.in0(rULA_2), .in1(data_2), .out(multiplexer_2_out), .sel(MemtoReg));
  Multiplexer #(.width(2)) multiplexer_3 (.in0(ra_2), .in1(2'b00), .out(rd), .sel(ALUSrc));
  banco_de_registradores banco_de_registradores_1 (
    .clk(clk), .RegWrite(RegWr), .Dado(multiplexer_2_out), .rd(rd_4), .Reset(Reset_out), .ALUSrc(ALUSrc),
    .rb(pipeline1_1_out_9), .saida_2(banco_de_registradores_1_saida_2),
    .saida_1(banco_de_registradores_1_saida_1));
  unidade_de_controle unidade_de_controle_1 (
    .opcode(opcode), .ALUSrc(ALUSrc), .Branch(Branch), .RegWr(RegWr), .MemtoReg(MemtoReg),
    .PcSumSrc(PCSumSrc), .Incr(Incr), .ALUOp(ALUOp));
  pipeline2 pipeline2_1 (
    .incr(Incr), .aluop(ALUOp), .alusrc(ALUSrc), .rb(banco_de_registradores_1_saida_2),
    .ra(banco_de_registradores_1_saida_1), .imm(Imm), .rd(rd), .opcode(opcode), .PC(PC_2), .branch(Branch),
    .clk(clk), .reset(PCSrc), .out_20(Incr_2), .out_21(ALUOp_2), .out_22(ALUSrc_2), .out_14(rb), .out_15(ra),
    .out_16(Imm_2), .out_17(rd_2), .out_18(opcode_2), .out_13(PC_3), .out_19(Branch_2));
  Multiplexer #(.width(8)) multiplexer_4 (.in0(rb), .in1(Imm_2), .out(multiplexer_4_out), .sel(ALUSrc_2));
  Adder adder_2 (.a(PC_3), .b(Imm_2), .out(adder_2_out), .cin(1'b0));  // open: cout
  and and_2 (salto, Branch_2, Zero);
  Multiplexer #(.width(8)) multiplexer_5 (.in0(adder_2_out), .in1(rb), .out(multiplexer_5_out), .sel(salto));
  ULA ula_1 (
    .Branch(Branch_2), .Incr(Incr_2), .rb(multiplexer_4_out), .ra(ra), .ALUOp(ALUOp_2), .out_7(ula_1_out_7),
    .zero(Zero));
  pipeline3 pipeline3_1 (
    .clk(clk), .TA(multiplexer_5_out), .rULA(ula_1_out_7), .ra(ra), .rb(rb), .PC(PC_3), .rd(rd_2),
    .opcode(opcode_2), .out_10(TA), .out_11(rULA), .out_12(ra_3), .out_13(rb_2), .out_9(PC_4), .out_14(rd_3),
    .op_out(opcode_3));
  pipeline4 pipeline4_1 (
    .mem(data), .rd(rd_3), .opcode(opcode_3), .rb(rb_2), .rULA(rULA), .clk(clk), .out_8(data_2),
    .out_9(rd_4), .out_10(opcode_4), .out_11(rb_3), .out_7(rULA_2));

  // Other names for the same wires on the sheet: PC[7:0] = out_1
endmodule

module PC_e_MI (
  input  [7:0] addr,
  input  [7:0] PC,
  input  clk,
  input  [7:0] d,
  output [7:0] instr,
  output [7:0] data,
  output [7:0] out_7
);

  wire and_1_out, button_1_out, not_1_out, not_2_out;

  Register register_1 (.D(PC), .en(1'b1), .clk(clk), .Q(out_7), .clr(button_1_out));
  Button button_1 (.out(button_1_out));
  not not_1 (not_1_out, instr[6]);
  not not_2 (not_2_out, instr[7]);
  and and_1 (and_1_out, instr[4], instr[5], not_1_out, not_2_out);
  dual_port_ram dual_port_ram_1 (.addr(addr), .pc(out_7), .d(d), .w(and_1_out), .clk(clk), .instr(instr), .data(data));
endmodule

module dual_port_ram (
  input  [7:0] addr,
  input  [7:0] pc,
  input  [7:0] d,
  input  w,
  input  clk,
  output [7:0] instr,
  output [7:0] data
);

  wire or_1_out;
  wire [7:0] multiplexer_1_out;

  or or_1 (or_1_out, w, clk);
  Multiplexer #(.width(8)) multiplexer_1 (.in0(addr), .in1(pc), .out(multiplexer_1_out), .sel(clk));
  RAM #(.asyncread("true")) ram_1 (.addr(multiplexer_1_out), .we(or_1_out), .oe(1'b1), .clk(clk), .din(d), .dout(data));
  Register #(.trigger("falling")) pcbuf (.D(data), .en(1'b1), .clk(clk), .Q(instr));  // open: clr
endmodule

module banco_de_registradores (
  input  Reset,
  input  [7:0] Dado,
  input  RegWrite,
  input  [1:0] rb,
  input  [1:0] rd,
  input  clk,
  input  ALUSrc,
  output [7:0] saida_2,
  output [7:0] saida_1
);

  wire demultiplexer_1_out0, demultiplexer_1_out1, demultiplexer_1_out2, demultiplexer_1_out3;
  wire [7:0] r0, r1, r2, r3;

  Demultiplexer #(.select(2)) demultiplexer_1 (
    .out0(demultiplexer_1_out0), .out1(demultiplexer_1_out1), .out2(demultiplexer_1_out2),
    .out3(demultiplexer_1_out3), .in(RegWrite), .sel(rd));
  Register u_r0 (.D(Dado), .en(demultiplexer_1_out0), .clk(clk), .Q(r0), .clr(Reset));
  Register u_r1 (.D(Dado), .en(demultiplexer_1_out1), .clk(clk), .Q(r1), .clr(Reset));
  Register u_r2 (.D(Dado), .en(demultiplexer_1_out2), .clk(clk), .Q(r2), .clr(Reset));
  Register u_r3 (.D(Dado), .en(demultiplexer_1_out3), .clk(clk), .Q(r3), .clr(Reset));
  Multiplexer #(.select(2), .width(8)) multiplexer_1 (.in0(r0), .in1(r1), .in2(r2), .in3(r3), .out(saida_2), .sel(rb));
  Multiplexer #(.select(2), .width(8)) multiplexer_2 (.in0(r0), .in1(r1), .in2(r2), .in3(r3), .out(saida_1), .sel(rd));

  // Other names for the same wires on the sheet: D[7:0] = Dado
endmodule

module ULA (
  input  [7:0] rb,
  input  [7:0] ra,
  input  Branch,
  input  Incr,
  input  [3:0] ALUOp,
  output zero,
  output [7:0] out_7
);

  wire comparator_2_eq, Shift;
  wire [2:0] multiplexer_2_out;
  wire [4:0] multiplexer_2_out_2;
  wire [7:0] adder_1_out, and_1_out, bit_extender_1_out, multiplexer_1_out, multiplexer_3_out,
       multiplexer_4_out, multiplier_1_out, or_1_out, shifter_1_out, shifter_2_out, subtractor_1_out,
       xor_1_out;

  Multiplexer #(.width(8)) multiplexer_1 (.in0(rb), .in1({8{1'b0}}), .out(multiplexer_1_out), .sel(Branch));
  Multiplexer #(.width(8)) multiplexer_2 (
    .in0(multiplexer_1_out), .in1(8'h1), .out({multiplexer_2_out_2, multiplexer_2_out}), .sel(Incr));
  Comparator comparator_1 (.a({multiplexer_2_out_2, multiplexer_2_out}), .b(8'h7), .gt(Shift));  // open: eq, lt
  Shifter shifter_1 (.in(ra), .\dist (multiplexer_2_out), .out(shifter_1_out));
  Shifter #(.shift("lr")) shifter_2 (.in(ra), .\dist (multiplexer_2_out), .out(shifter_2_out));
  Adder adder_1 (.a(ra), .b({multiplexer_2_out_2, multiplexer_2_out}), .out(adder_1_out));  // open: cin, cout
  Subtractor subtractor_1 (
    .a(ra), .b({multiplexer_2_out_2, multiplexer_2_out}), .out(subtractor_1_out));  // open: bin, bout
  Comparator comparator_2 (
    .a({multiplexer_2_out_2, multiplexer_2_out}), .b({8{1'b0}}), .eq(comparator_2_eq));  // open: gt, lt
  assign and_1_out = ra & {multiplexer_2_out_2, multiplexer_2_out};  // AND_Gate and_1, 8 bits wide
  assign or_1_out = ra | {multiplexer_2_out_2, multiplexer_2_out};  // OR_Gate or_1, 8 bits wide
  assign xor_1_out = ra ^ {multiplexer_2_out_2, multiplexer_2_out};  // XOR_Gate xor_1, 8 bits wide
  Multiplexer #(.width(8)) multiplexer_3 (.in0(shifter_1_out), .in1({8{1'b0}}), .out(multiplexer_3_out), .sel(Shift));
  Multiplexer #(.width(8)) multiplexer_4 (.in0(shifter_2_out), .in1({8{1'b0}}), .out(multiplexer_4_out), .sel(Shift));
  Multiplier multiplier_1 (
    .a(ra), .b({multiplexer_2_out_2, multiplexer_2_out}), .out(multiplier_1_out));  // open: cin, cout
  assign bit_extender_1_out = {{7{1'b0}}, comparator_2_eq};  // Bit_Extender bit_extender_1
  Multiplexer #(.select(4), .width(8)) multiplexer_5 (
    .in0(adder_1_out), .in1(subtractor_1_out), .in2(bit_extender_1_out), .in3(and_1_out), .in4(or_1_out),
    .in5(xor_1_out), .in6(multiplexer_3_out), .in7(multiplexer_4_out), .in8(multiplier_1_out),
    .in9({multiplexer_2_out_2, multiplexer_2_out}), .out(out_7), .sel(ALUOp));  // open: in10, in11, in12, in13, in14, in15
  Comparator comparator_3 (.a({8{1'b0}}), .b(out_7), .eq(zero));  // open: gt, lt

  // Notes on the sheet:
  //   para (ra - 0)
  //   mv
endmodule

module unidade_de_controle (
  input  [3:0] opcode,
  output [3:0] ALUOp,
  output ALUSrc,
  output Branch,
  output RegWr,
  output MemtoReg,
  output PcSumSrc,
  output Incr
);

  wire and_1_out, and_2_out, and_4_out, and_5_out, and_6_out, and_7_out, and_8_out, and_11_out, not_1_out,
       not_2_out, not_3_out, not_4_out;

  not not_1 (not_1_out, opcode[3]);
  not not_2 (not_2_out, opcode[2]);
  not not_3 (not_3_out, opcode[1]);
  not not_4 (not_4_out, opcode[0]);
  and and_1 (and_1_out, not_1_out, opcode[2], not_3_out, opcode[0]);
  or or_1 (ALUOp[3], and_1_out, and_2_out);
  and and_2 (and_2_out, not_1_out, opcode[2], opcode[1], not_4_out);
  and and_3 (ALUOp[2], opcode[3], opcode[1]);
  and and_4 (and_4_out, opcode[3], not_2_out, not_3_out);
  or or_2 (ALUOp[1], and_4_out, and_5_out);
  and and_5 (and_5_out, opcode[3], opcode[2], opcode[1]);
  and and_6 (and_6_out, not_1_out, not_2_out, not_3_out, not_4_out);
  and and_7 (and_7_out, not_1_out, opcode[2], opcode[1], not_4_out);
  or or_3 (ALUOp[0], and_6_out, and_7_out, and_8_out);
  and and_8 (and_8_out, opcode[3], opcode[0]);
  and and_9 (ALUSrc, not_1_out, opcode[2], not_3_out);
  and and_10 (Branch, not_4_out, not_3_out, not_2_out, not_1_out);
  and and_11 (and_11_out, opcode[1], not_4_out);
  or or_4 (RegWr, and_11_out, opcode[2], opcode[3]);
  and and_12 (MemtoReg, not_1_out, not_2_out, opcode[1], not_4_out);
  and and_13 (PcSumSrc, not_1_out, not_2_out, not_3_out, opcode[0]);
  and and_14 (Incr, not_1_out, opcode[2], opcode[1], opcode[0]);
endmodule

module pipeline1 (
  input  [7:0] PC,
  input  clk,
  input  [1:0] rb,
  input  [1:0] ra,
  input  reset,
  input  [3:0] imm,
  input  [3:0] opcode,
  output [7:0] out_8,
  output [1:0] out_9,
  output [1:0] out_10,
  output [3:0] out_11,
  output [3:0] out_12
);

  Register register_1 (.D(PC), .en(1'b1), .clk(clk), .Q(out_8), .clr(reset));
  Register #(.width(2)) register_2 (.D(rb), .en(1'b1), .clk(clk), .Q(out_9), .clr(reset));
  Register #(.width(2)) register_3 (.D(ra), .en(1'b1), .clk(clk), .Q(out_10), .clr(reset));
  Register #(.width(4)) register_4 (.D(imm), .en(1'b1), .clk(clk), .Q(out_11), .clr(reset));
  Register #(.width(4)) register_5 (.D(opcode), .en(1'b1), .clk(clk), .Q(out_12), .clr(reset));
endmodule

module pipeline2 (
  input  [7:0] PC,
  input  clk,
  input  [7:0] rb,
  input  [7:0] ra,
  input  reset,
  input  [7:0] imm,
  input  [1:0] rd,
  input  [3:0] opcode,
  input  branch,
  input  incr,
  input  [3:0] aluop,
  input  alusrc,
  output [7:0] out_13,
  output [7:0] out_14,
  output [7:0] out_15,
  output [7:0] out_16,
  output [1:0] out_17,
  output [3:0] out_18,
  output out_19,
  output out_20,
  output [3:0] out_21,
  output out_22
);

  Register register_1 (.D(PC), .en(1'b1), .clk(clk), .Q(out_13), .clr(reset));
  Register register_2 (.D(rb), .en(1'b1), .clk(clk), .Q(out_14), .clr(reset));
  Register register_3 (.D(ra), .en(1'b1), .clk(clk), .Q(out_15), .clr(reset));
  Register register_4 (.D(imm), .en(1'b1), .clk(clk), .Q(out_16), .clr(reset));
  Register #(.width(2)) register_5 (.D(rd), .en(1'b1), .clk(clk), .Q(out_17), .clr(reset));
  Register #(.width(4)) register_6 (.D(opcode), .en(1'b1), .clk(clk), .Q(out_18), .clr(reset));
  Register #(.width(1)) register_7 (.D(branch), .en(1'b1), .clk(clk), .Q(out_19), .clr(reset));
  Register #(.width(1)) register_8 (.D(incr), .en(1'b1), .clk(clk), .Q(out_20), .clr(reset));
  Register #(.width(4)) register_9 (.D(aluop), .en(1'b1), .clk(clk), .Q(out_21), .clr(reset));
  Register #(.width(1)) register_10 (.D(alusrc), .en(1'b1), .clk(clk), .Q(out_22), .clr(reset));
endmodule

module pipeline3 (
  input  [7:0] PC,
  input  clk,
  input  [7:0] TA,
  input  [7:0] rULA,
  input  [7:0] ra,
  input  [7:0] rb,
  input  [1:0] rd,
  input  [3:0] opcode,
  output [7:0] out_9,
  output [7:0] out_10,
  output [7:0] out_11,
  output [7:0] out_12,
  output [7:0] out_13,
  output [1:0] out_14,
  output [3:0] op_out
);

  Register register_1 (.D(PC), .en(1'b1), .clk(clk), .Q(out_9));  // open: clr
  Register register_2 (.D(TA), .en(1'b1), .clk(clk), .Q(out_10));  // open: clr
  Register register_3 (.D(rULA), .en(1'b1), .clk(clk), .Q(out_11));  // open: clr
  Register register_4 (.D(ra), .en(1'b1), .clk(clk), .Q(out_12));  // open: clr
  Register register_5 (.D(rb), .en(1'b1), .clk(clk), .Q(out_13));  // open: clr
  Register #(.width(2)) register_6 (.D(rd), .en(1'b1), .clk(clk), .Q(out_14));  // open: clr
  Register #(.width(4)) register_7 (.D(opcode), .en(1'b1), .clk(clk), .Q(op_out));  // open: clr
endmodule

module pipeline4 (
  input  [7:0] rULA,
  input  [7:0] mem,
  input  clk,
  input  [1:0] rd,
  input  [3:0] opcode,
  input  [7:0] rb,
  output [7:0] out_7,
  output [7:0] out_8,
  output [1:0] out_9,
  output [3:0] out_10,
  output [7:0] out_11
);

  Register register_1 (.D(rULA), .en(1'b1), .clk(clk), .Q(out_7));  // open: clr
  Register register_2 (.D(mem), .en(1'b1), .clk(clk), .Q(out_8));  // open: clr
  Register #(.width(2)) register_3 (.D(rd), .en(1'b1), .clk(clk), .Q(out_9));  // open: clr
  Register #(.width(4)) register_4 (.D(opcode), .en(1'b1), .clk(clk), .Q(out_10));  // open: clr
  Register register_5 (.D(rb), .en(1'b1), .clk(clk), .Q(out_11));  // open: clr
endmodule
