// Logisim project vetorial.circ as structural Verilog: 5 circuits, main circuit main
module main (
  input  [7:0] in_1,
  input  [7:0] in_2,
  input  [7:0] in_3,
  output [7:0] out_4,
  output [7:0] out_5,
  output [7:0] out_6
);

  wire alusrc, and_1_out, branch, clk, memread, memwrite, memwrite_SPE, memwrite_VPE, regwrite, regwrite_SPE,
       regwrite_VPE, reset, sel_vpe, zero;
  wire [3:0] aluop;
  wire [7:0] adder_1_out, endereco, imediato, multiplexer_1_out, multiplexer_2_out, multiplexer_3_out,
       multiplexer_4_out, pc, saidaA, saidaMEM, saidamem_t, saidaULA, vr1;

  Adder adder_1 (.a(8'h1), .b(pc), .out(adder_1_out));  // open: cin, cout
  and and_1 (and_1_out, branch, zero);
  Multiplexer #(.width(8)) multiplexer_1 (.in0(adder_1_out), .in1(endereco), .out(multiplexer_1_out), .sel(and_1_out));
  Clock clock_1 (.out(clk));
  Button button_1 (.out(reset));
  Register u_PC (.D(multiplexer_1_out), .en(1'b1), .clk(clk), .Q(pc), .clr(reset));
  RAM #(.asyncread("true")) ram_1 (.addr(pc), .we(1'b0), .oe(1'b1), .clk(clk), .din({8{1'b0}}), .dout(out_4));
  // NoConnect on nothing
  assign imediato = {{4{out_4[3]}}, out_4[3:0]};  // Bit_Extender bit_extender_1
  and and_2 (regwrite_VPE, regwrite, sel_vpe);
  and and_3 (regwrite_SPE, regwrite, ~sel_vpe);  // AND_Gate
  and and_4 (memwrite_VPE, memwrite, sel_vpe);
  and and_5 (memwrite_SPE, memwrite, ~sel_vpe);  // AND_Gate
  UC uc_1 (
    .opcode(out_4[7:4]), .branch(branch), .memwrite(memwrite), .memread(memread), .aluop(aluop),
    .regwrite(regwrite), .sel_vpe(sel_vpe), .alusrc(alusrc));
  PE pe_1 (
    .PE_ID({8{1'b0}}), .Ra(out_4[3:2]), .aluop_V(aluop), .regwrite_V(regwrite_VPE), .wbSel(alusrc),
    .Rb(out_4[1:0]), .memwrite_V(memwrite_VPE), .memread(memread), .clock(clk), .reset(reset), .VR1_out(in_1));  // open: aluout, VR2_out, memout, VR3_out
  PE pe_2 (
    .PE_ID(8'h1), .Ra(out_4[3:2]), .aluop_V(aluop), .regwrite_V(regwrite_VPE), .wbSel(alusrc),
    .Rb(out_4[1:0]), .memwrite_V(memwrite_VPE), .memread(memread), .clock(clk), .reset(reset), .VR1_out(in_2));  // open: aluout, VR2_out, memout, VR3_out
  PE pe_3 (
    .PE_ID(8'h2), .Ra(out_4[3:2]), .aluop_V(aluop), .regwrite_V(regwrite_VPE), .wbSel(alusrc),
    .Rb(out_4[1:0]), .memwrite_V(memwrite_VPE), .memread(memread), .clock(clk), .reset(reset), .VR1_out(out_5));  // open: aluout, VR2_out, memout, VR3_out
  PE pe_4 (
    .PE_ID(8'h3), .Ra(out_4[3:2]), .aluop_V(aluop), .regwrite_V(regwrite_VPE), .wbSel(alusrc),
    .Rb(out_4[1:0]), .memwrite_V(memwrite_VPE), .memread(memread), .clock(clk), .reset(reset), .VR1_out(out_6));  // open: aluout, VR2_out, memout, VR3_out
  Multiplexer #(.width(8)) multiplexer_2 (.in0(saidaULA), .in1(saidaMEM), .out(multiplexer_2_out), .sel(memread));
  Multiplexer #(.width(8)) multiplexer_3 (.in0(endereco), .in1(imediato), .out(multiplexer_3_out), .sel(alusrc));
  Multiplexer #(.width(8)) multiplexer_4 (.in0(saidaA), .in1(vr1), .out(multiplexer_4_out), .sel(alusrc));
  RAM ram_2 (.addr(endereco), .we(memwrite_SPE), .oe(memread), .clk(clk), .dout(saidamem_t));  // open: din
  banco_SPE banco_spe_1 (
    .data_in(multiplexer_2_out), .reset(reset), .regwrite(regwrite_SPE), .Ra(out_4[3:2]), .r1(alusrc),
    .Rb(out_4[1:0]), .clock(clk), .saidaA(saidaA), .vr1(vr1), .saidaB(endereco));
  ULA ula_1 (.A(multiplexer_4_out), .B(multiplexer_3_out), .aluop(aluop), .zero(zero), .saida(saidaULA));

  // Other names for the same wires on the sheet: instrucao[7:0] = out_4; opcode[3:0] = out_4[7:4];
  //   imm[3:0] = out_4[3:0]; ra[1:0] = out_4[3:2]; rb[1:0] = out_4[1:0]; saidaB[7:0] = endereco
endmodule

module UC (
  input  [3:0] opcode,
  output branch,
  output memwrite,
  output memread,
  output [3:0] aluop,
  output regwrite,
  output sel_vpe,
  output alusrc
);

  ROM #(.addrWidth(4), .dataWidth(10)) rom_1 (
    .addr(opcode), .data({alusrc, sel_vpe, regwrite, aluop, memread, memwrite, branch}));

  // Notes on the sheet:
  //   contents of rom_1 (hex, n*v repeats v):
  //   84 2 2c8 2c0 80 88 90 9 184 102 3c8 3c0 180 188 2d0 3d0
endmodule

module ULA (
  input  [7:0] A,
  input  [7:0] B,
  input  [3:0] aluop,
  output zero,
  output [7:0] saida
);

  wire zera;
  wire [7:0] adder_1_out, and_2_out, multiplexer_1_out, multiplexer_2_out, negator_1_out, or_2_out,
       shifter_1_out, shifter_2_out, subtractor_1_out, xor_1_out;

  or or_1 (zera, B[7], B[6], B[5], B[4], B[3]);
  and and_1 (zero, ~1'b0, ~A[0], ~A[1], ~A[2], ~A[3], ~A[4], ~A[5], ~A[6], ~A[7]);  // AND_Gate
  Adder adder_1 (.a(A), .b(B), .out(adder_1_out));  // open: cin, cout
  Subtractor subtractor_1 (.a(A), .b(B), .out(subtractor_1_out));  // open: bin, bout
  assign and_2_out = A & B;  // AND_Gate and_2, 8 bits wide
  assign or_2_out = A | B;  // OR_Gate or_2, 8 bits wide
  assign xor_1_out = A ^ B;  // XOR_Gate xor_1, 8 bits wide
  Negator negator_1 (.in(A), .out(negator_1_out));
  Shifter shifter_1 (.in(A), .\dist (B[2:0]), .out(shifter_1_out));
  Shifter shifter_2 (.in(A), .\dist (B[2:0]), .out(shifter_2_out));
  Multiplexer #(.width(8)) multiplexer_1 (.in0(negator_1_out), .in1({8{1'b0}}), .out(multiplexer_1_out), .sel(zera));
  Multiplexer #(.width(8)) multiplexer_2 (.in0(shifter_1_out), .in1({8{1'b0}}), .out(multiplexer_2_out), .sel(zera));
  Multiplexer #(.select(4), .width(8)) multiplexer_3 (
    .in0(adder_1_out), .in1(subtractor_1_out), .in2(and_2_out), .in3(or_2_out), .in4(xor_1_out),
    .in5(multiplexer_1_out), .in6(multiplexer_2_out), .in7(shifter_2_out), .in8({A[7:4], B[3:0]}),
    .in9({B[3:0], A[3:0]}), .in10(adder_1_out), .out(saida), .sel(aluop));  // open: in11, in12, in13, in14, in15

  // Other names for the same wires on the sheet: altos[3:0] = A[7:4]; baixos[3:0] = A[3:0]
endmodule

module banco_SPE (
  input  [7:0] data_in,
  input  reset,
  input  regwrite,
  input  [1:0] Ra,
  input  r1,
  input  [1:0] Rb,
  input  clock,
  output [7:0] saidaA,
  output [7:0] vr1,
  output [7:0] saidaB
);

  wire demultiplexer_1_out1, demultiplexer_1_out2, demultiplexer_1_out3;
  wire [1:0] multiplexer_1_out;
  wire [7:0] SR0_q, SR2_q, SR3_q;

  Demultiplexer #(.select(2)) demultiplexer_1 (
    .out1(demultiplexer_1_out1), .out2(demultiplexer_1_out2), .out3(demultiplexer_1_out3), .in(regwrite),
    .sel(multiplexer_1_out));  // open: out0
  Multiplexer #(.width(2)) multiplexer_1 (.in0(Ra), .in1(2'b01), .out(multiplexer_1_out), .sel(r1));
  Register SR0 (.D({8{1'b0}}), .en(1'b1), .clk(clock), .Q(SR0_q), .clr(reset));
  Register SR1 (.D(data_in), .en(demultiplexer_1_out1), .clk(clock), .Q(vr1), .clr(reset));
  Register SR2 (.D(data_in), .en(demultiplexer_1_out2), .clk(clock), .Q(SR2_q), .clr(reset));
  Register SR3 (.D(data_in), .en(demultiplexer_1_out3), .clk(clock), .Q(SR3_q), .clr(reset));
  Multiplexer #(.select(2), .width(8)) multiplexer_2 (
    .in0(SR0_q), .in1(vr1), .in2(SR2_q), .in3(SR3_q), .out(saidaA), .sel(Ra));
  Multiplexer #(.select(2), .width(8)) multiplexer_3 (
    .in0(SR0_q), .in1(vr1), .in2(SR2_q), .in3(SR3_q), .out(saidaB), .sel(Rb));
endmodule

module PE (
  input  [7:0] PE_ID,
  input  [1:0] Ra,
  input  [3:0] aluop_V,
  input  regwrite_V,
  input  wbSel,
  input  [1:0] Rb,
  input  memwrite_V,
  input  memread,
  input  clock,
  input  reset,
  output [7:0] VR1_out,
  output [7:0] aluout,
  output [7:0] VR2_out,
  output [7:0] memout,
  output [7:0] VR3_out
);

  wire demultiplexer_1_out1, demultiplexer_1_out2, demultiplexer_1_out3;
  wire [1:0] multiplexer_1_out;
  wire [7:0] dado, imediato, multiplexer_4_out, multiplexer_5_out, readA, readB, VR0_q;

  Demultiplexer #(.select(2)) demultiplexer_1 (
    .out1(demultiplexer_1_out1), .out2(demultiplexer_1_out2), .out3(demultiplexer_1_out3), .in(regwrite_V),
    .sel(multiplexer_1_out));  // open: out0
  Multiplexer #(.width(2)) multiplexer_1 (.in0(Ra), .in1(2'b01), .out(multiplexer_1_out), .sel(aluop_V[3]));
  Register VR0 (.D(PE_ID), .en(1'b1), .clk(clock), .Q(VR0_q));  // open: clr
  Register VR1 (.D(dado), .en(demultiplexer_1_out1), .clk(clock), .Q(VR1_out), .clr(reset));
  Register VR2 (.D(dado), .en(demultiplexer_1_out2), .clk(clock), .Q(VR2_out), .clr(reset));
  Register VR3 (.D(dado), .en(demultiplexer_1_out3), .clk(clock), .Q(VR3_out), .clr(reset));
  Multiplexer #(.select(2), .width(8)) multiplexer_2 (
    .in0(VR0_q), .in1(VR1_out), .in2(VR2_out), .in3(VR3_out), .out(readA), .sel(Ra));
  Multiplexer #(.select(2), .width(8)) multiplexer_3 (
    .in0(VR0_q), .in1(VR1_out), .in2(VR2_out), .in3(VR3_out), .out(readB), .sel(Rb));
  Multiplexer #(.width(8)) multiplexer_4 (.in0(readB), .in1(imediato), .out(multiplexer_4_out), .sel(aluop_V[3]));
  assign imediato = {{4{Ra[1]}}, {Ra, Rb}};  // Bit_Extender bit_extender_1
  Multiplexer #(.width(8)) multiplexer_5 (.in0(readA), .in1(VR1_out), .out(multiplexer_5_out), .sel(aluop_V[3]));
  ULA ula_1 (.A(multiplexer_5_out), .B(multiplexer_4_out), .aluop(aluop_V), .saida(aluout));  // open: zero
  RAM #(.asyncread("true")) ram_1 (
    .addr(readB), .we(memwrite_V), .oe(memread), .clk(clock), .din(readA), .dout(memout));
  Multiplexer #(.width(8)) multiplexer_6 (.in0(aluout), .in1(memout), .out(dado), .sel(memread));

  // Other names for the same wires on the sheet: r1 = aluop_V[3]; clk = clock; mem = memread; VR1[7:0] = VR1_out
endmodule
