// Logisim project trabalho_3_pipeline.circ as structural Verilog: 10 circuits, main circuit PC_e_MI
module trabalho (
  output [7:0] out_1
);

  wire ALUSrc, ALUSrc_2, and_1_out, Branch, Branch_2, Branch_3, clk, comparator_1_gt, Incr, Incr_2, JumpImm,
       JumpImm_2, JumpImm_3, MemtoReg, MemtoReg_2, MemtoReg_3, MemtoReg_4, MemWr, MemWr_2, MemWr_3,
       not_1_out, not_2_out, PcSrc, RegWr, RegWr_2, RegWr_3, RegWr_4, Reset_out, Zero, Zero_2;
  wire [1:0] pipeline1_1_out_10, pipeline1_1_out_11, rd, rd_2, rd_3, rd_4;
  wire [3:0] ALUOp, ALUOp_2, opcode, opcode_2, opcode_3, opcode_4, pipeline1_1_out_12, undriven, undriven_2;
  wire [7:0] adder_1_out, adder_2_out, banco_de_registradores_1_saida_ra, banco_de_registradores_1_saida_rb,
       bit_extender_2_out, data, data_2, data_3, data_4, data_5, Imm, Imm_2, multiplexer_1_out,
       multiplexer_2_out, multiplexer_4_out, multiplexer_5_out, PC_2, PC_3, PC_4, ra, ra_2, rb, rb_2, rULA,
       rULA_2, TA, ula_1_out_7;
  wire [31:0] pc_e_mi_1_instr;

  Adder adder_1 (.a(out_1), .b(8'h1), .out(adder_1_out), .cin(1'b0));  // open: cout
  Multiplexer #(.width(8)) multiplexer_1 (.in0(adder_1_out), .in1(TA), .out(multiplexer_1_out), .sel(PcSrc));
  not not_1 (not_1_out, clk);
  Clock clock_1 (.out(clk));
  PC_e_MI pc_e_mi_1 (
    .clk(not_1_out), .PC(multiplexer_1_out), .d(ra_2), .MemWr(MemWr_3), .addr(rb_2), .out_7(out_1),
    .instr(pc_e_mi_1_instr), .data(data));
  pipeline1 pipeline1_1 (
    .clk(clk), .reset(PcSrc), .rb(undriven_2[1:0]), .ra(undriven_2[3:2]), .imm(undriven_2),
    .opcode(undriven), .data(data), .PC(out_1), .out_10(pipeline1_1_out_10), .out_11(pipeline1_1_out_11),
    .out_12(pipeline1_1_out_12), .out_13(opcode), .out_14(data_2), .out_9(PC_2));
  Button Reset (.out(Reset_out));
  assign Imm = {{4{pipeline1_1_out_12[3]}}, pipeline1_1_out_12};  // Bit_Extender bit_extender_1
  not not_2 (not_2_out, clk);
  Multiplexer #(.width(8)) multiplexer_2 (.in0(rULA_2), .in1(data), .out(multiplexer_2_out), .sel(MemtoReg_4));
  Multiplexer #(.width(2)) multiplexer_3 (.in0(pipeline1_1_out_11), .in1(2'b00), .out(rd), .sel(ALUSrc));
  unidade_de_controle unidade_de_controle_1 (
    .opcode(opcode), .ALUSrc(ALUSrc), .Branch(Branch), .RegWr(RegWr), .MemtoReg(MemtoReg), .JumpImm(JumpImm),
    .Incr(Incr), .MemWr(MemWr), .ALUOp(ALUOp));
  banco_de_registradores banco_de_registradores_1 (
    .clk(not_2_out), .RegWrite(RegWr_4), .Dado(multiplexer_2_out), .rd(rd_4), .Reset(Reset_out),
    .rb(pipeline1_1_out_10), .ra(rd), .saida_rb(banco_de_registradores_1_saida_rb),
    .saida_ra(banco_de_registradores_1_saida_ra));
  pipeline2 pipeline2_1 (
    .MemtoReg(MemtoReg), .opcode(opcode), .branch(Branch), .incr(Incr), .RegWr(RegWr), .ALUOp(ALUOp),
    .PCSrc(JumpImm), .ALUSrc(ALUSrc), .MemWr(MemWr), .data(data_2), .PC(PC_2),
    .rb(banco_de_registradores_1_saida_rb), .ra(banco_de_registradores_1_saida_ra), .imm(Imm), .rd(rd),
    .clk(clk), .reset(PcSrc), .out_18(MemtoReg_2), .out_25(opcode_2), .out_26(Branch_2), .out_27(Incr_2),
    .out_28(RegWr_2), .out_29(ALUOp_2), .out_30(JumpImm_2), .out_31(ALUSrc_2), .out_32(MemWr_2),
    .out_19(data_3), .out_20(PC_3), .out_21(rb), .out_22(ra), .out_23(Imm_2), .out_24(rd_2));
  Multiplexer #(.width(8)) multiplexer_4 (.in0(rb), .in1(Imm_2), .out(multiplexer_4_out), .sel(ALUSrc_2));
  Adder adder_2 (.a(PC_3), .b(Imm_2), .out(adder_2_out), .cin(1'b0));  // open: cout
  Multiplexer #(.width(8)) multiplexer_5 (.in0(rb), .in1(adder_2_out), .out(multiplexer_5_out), .sel(JumpImm_2));
  ULA ula_1 (
    .Branch(Branch_2), .Incr(Incr_2), .rb(multiplexer_4_out), .ra(ra), .ALUOp(ALUOp_2), .out_7(ula_1_out_7),
    .zero(Zero));
  pipeline3 pipeline3_1 (
    .clk(clk), .reset(PcSrc), .zero(Zero), .JumpImm(JumpImm_2), .MemtoReg(MemtoReg_2), .ALUSrc(RegWr_2),
    .branch(Branch_2), .MemWr(MemWr_2), .PC(PC_3), .TA(multiplexer_5_out), .rULA(ula_1_out_7), .ra(ra),
    .rb(rb), .rd(rd_2), .out_22(Zero_2), .out_23(JumpImm_3), .out_24(MemtoReg_3), .out_25(RegWr_3),
    .out_15(Branch_3), .out_26(MemWr_3), .out_16(PC_4), .out_17(TA), .out_18(rULA), .out_19(ra_2),
    .out_20(rb_2), .out_21(rd_3));
  assign bit_extender_2_out = {{7{1'b0}}, 1'b0};  // Bit_Extender bit_extender_2
  Comparator comparator_1 (.a(PC_4), .b(bit_extender_2_out), .gt(comparator_1_gt));  // open: eq, lt
  and and_1 (and_1_out, comparator_1_gt, Zero_2, Branch_3);
  or or_1 (PcSrc, and_1_out, JumpImm_3);
  pipeline4 pipeline4_1 (
    .MemtoReg(MemtoReg_3), .mem(data_4), .rd(rd_3), .opcode(opcode_3), .data(data_4), .rULA(rULA),
    .RegWr(RegWr_3), .clk(clk), .reset(PcSrc), .out_16(MemtoReg_4), .out_11(data_5), .out_12(rd_4),
    .out_13(opcode_4), .out_14(data_5), .out_10(rULA_2), .out_15(RegWr_4));

  // Other names for the same wires on the sheet: PC[7:0] = out_1
endmodule

module PC_e_MI (
  input  [7:0] addr,
  input  [7:0] PC,
  input  clk,
  input  MemWr,
  input  [7:0] d,
  output [31:0] instr,
  output [7:0] out_7,
  output [7:0] data
);

  wire button_1_out;
  wire [31:0] bit_extender_1_out;
  wire [31:8] dual_port_ram_1_data;

  Register register_1 (.D(PC), .en(1'b1), .clk(clk), .Q(out_7), .clr(button_1_out));
  Button button_1 (.out(button_1_out));
  assign bit_extender_1_out = {{24{1'b0}}, d};  // Bit_Extender bit_extender_1
  dual_port_ram dual_port_ram_1 (
    .addr(addr), .pc(out_7), .d(bit_extender_1_out), .w(MemWr), .clk(clk), .instr(instr),
    .data({dual_port_ram_1_data, data}));
endmodule

module dual_port_ram (
  input  [7:0] addr,
  input  [7:0] pc,
  input  [31:0] d,
  input  w,
  input  clk,
  output [31:0] instr,
  output [31:0] data
);

  wire or_1_out;
  wire [7:0] multiplexer_1_out;

  or or_1 (or_1_out, w, clk);
  Multiplexer #(.width(8)) multiplexer_1 (.in0(addr), .in1(pc), .out(multiplexer_1_out), .sel(clk));
  RAM #(.asyncread("true"), .dataWidth(32)) ram_1 (
    .addr(multiplexer_1_out), .we(or_1_out), .oe(1'b1), .clk(clk), .din(d), .dout(data));
  Register #(.trigger("falling"), .width(32)) pcbuf (.D(data), .en(1'b1), .clk(clk), .Q(instr));  // open: clr
endmodule

module banco_de_registradores (
  input  Reset,
  input  [7:0] Dado,
  input  RegWrite,
  input  [1:0] rb,
  input  [1:0] rd,
  input  clk,
  input  [1:0] ra,
  output [7:0] saida_rb,
  output [7:0] saida_ra
);

  wire demultiplexer_1_out0, demultiplexer_1_out1, demultiplexer_1_out2, demultiplexer_1_out3;
  wire [7:0] r0, r1, r2, r3;

  Demultiplexer #(.select(2)) demultiplexer_1 (
    .out0(demultiplexer_1_out0), .out1(demultiplexer_1_out1), .out2(demultiplexer_1_out2),
    .out3(demultiplexer_1_out3), .in(RegWrite), .sel(rd));
  Register u_r0 (.D(Dado), .en(demultiplexer_1_out0), .clk(clk), .Q(r0), .clr(Reset));
  Register u_r1 (.D(Dado), .en(demultiplexer_1_out1), .clk(clk), .Q(r1), .clr(Reset));
  Register u_r2 (.D(Dado), .en(demultiplexer_1_out2), .clk(clk), .Q(r2), .clr(Reset));
  Register u_r3 (.D(Dado), .en(demultiplexer_1_out3), .clk(clk), .Q(r3), .clr(Reset));
  Multiplexer #(.select(2), .width(8)) multiplexer_1 (.in0(r0), .in1(r1), .in2(r2), .in3(r3), .out(saida_rb), .sel(rb));
  Multiplexer #(.select(2), .width(8)) multiplexer_2 (.in0(r0), .in1(r1), .in2(r2), .in3(r3), .out(saida_ra), .sel(ra));

  // Other names for the same wires on the sheet: D[7:0] = Dado
endmodule

module ULA (
  input  [7:0] rb,
  input  [7:0] ra,
  input  Branch,
  input  Incr,
  input  [3:0] ALUOp,
  output zero,
  output [7:0] out_7
);

  wire comparator_2_eq, Shift;
  wire [2:0] multiplexer_2_out;
  wire [4:0] multiplexer_2_out_2;
  wire [7:0] adder_1_out, and_1_out, bit_extender_1_out, multiplexer_1_out, multiplexer_3_out,
       multiplexer_4_out, multiplier_1_out, or_1_out, shifter_1_out, shifter_2_out, subtractor_1_out,
       xor_1_out;

  Multiplexer #(.width(8)) multiplexer_1 (.in0(rb), .in1({8{1'b0}}), .out(multiplexer_1_out), .sel(Branch));
  Multiplexer #(.width(8)) multiplexer_2 (
    .in0(multiplexer_1_out), .in1(8'h1), .out({multiplexer_2_out_2, multiplexer_2_out}), .sel(Incr));
  Comparator comparator_1 (.a({multiplexer_2_out_2, multiplexer_2_out}), .b(8'h7), .gt(Shift));  // open: eq, lt
  Shifter shifter_1 (.in(ra), .\dist (multiplexer_2_out), .out(shifter_1_out));
  Shifter #(.shift("lr")) shifter_2 (.in(ra), .\dist (multiplexer_2_out), .out(shifter_2_out));
  Adder adder_1 (.a(ra), .b({multiplexer_2_out_2, multiplexer_2_out}), .out(adder_1_out));  // open: cin, cout
  Subtractor subtractor_1 (
    .a(ra), .b({multiplexer_2_out_2, multiplexer_2_out}), .out(subtractor_1_out));  // open: bin, bout
  Comparator comparator_2 (
    .a({multiplexer_2_out_2, multiplexer_2_out}), .b({8{1'b0}}), .eq(comparator_2_eq));  // open: gt, lt
  assign and_1_out = ra & {multiplexer_2_out_2, multiplexer_2_out};  // AND_Gate and_1, 8 bits wide
  assign or_1_out = ra | {multiplexer_2_out_2, multiplexer_2_out};  // OR_Gate or_1, 8 bits wide
  assign xor_1_out = ra ^ {multiplexer_2_out_2, multiplexer_2_out};  // XOR_Gate xor_1, 8 bits wide
  Multiplexer #(.width(8)) multiplexer_3 (.in0(shifter_1_out), .in1({8{1'b0}}), .out(multiplexer_3_out), .sel(Shift));
  Multiplexer #(.width(8)) multiplexer_4 (.in0(shifter_2_out), .in1({8{1'b0}}), .out(multiplexer_4_out), .sel(Shift));
  Multiplier multiplier_1 (
    .a(ra), .b({multiplexer_2_out_2, multiplexer_2_out}), .out(multiplier_1_out));  // open: cin, cout
  assign bit_extender_1_out = {{7{1'b0}}, comparator_2_eq};  // Bit_Extender bit_extender_1
  Multiplexer #(.select(4), .width(8)) multiplexer_5 (
    .in0(adder_1_out), .in1(subtractor_1_out), .in2(bit_extender_1_out), .in3(and_1_out), .in4(or_1_out),
    .in5(xor_1_out), .in6(multiplexer_3_out), .in7(multiplexer_4_out), .in8(multiplier_1_out),
    .in9({multiplexer_2_out_2, multiplexer_2_out}), .out(out_7), .sel(ALUOp));  // open: in10, in11, in12, in13, in14, in15
  Comparator comparator_3 (.a({8{1'b0}}), .b(out_7), .eq(zero));  // open: gt, lt

  // Notes on the sheet:
  //   para (ra - 0)
  //   mv
endmodule

module unidade_de_controle (
  input  [3:0] opcode,
  output [3:0] ALUOp,
  output ALUSrc,
  output Branch,
  output RegWr,
  output MemtoReg,
  output JumpImm,
  output Incr,
  output MemWr
);

  wire and_1_out, and_2_out, and_4_out, and_5_out, and_6_out, and_7_out, and_8_out, and_11_out, not_1_out,
       not_2_out, not_3_out, not_4_out;

  not not_1 (not_1_out, opcode[3]);
  not not_2 (not_2_out, opcode[2]);
  not not_3 (not_3_out, opcode[1]);
  not not_4 (not_4_out, opcode[0]);
  and and_1 (and_1_out, not_1_out, opcode[2], not_3_out, opcode[0]);
  or or_1 (ALUOp[3], and_1_out, and_2_out);
  and and_2 (and_2_out, not_1_out, opcode[2], opcode[1], not_4_out);
  and and_3 (ALUOp[2], opcode[3], opcode[1]);
  and and_4 (and_4_out, opcode[3], not_2_out, not_3_out);
  or or_2 (ALUOp[1], and_4_out, and_5_out);
  and and_5 (and_5_out, opcode[3], opcode[2], opcode[1]);
  and and_6 (and_6_out, not_1_out, not_2_out, not_3_out, not_4_out);
  and and_7 (and_7_out, not_1_out, opcode[2], opcode[1], not_4_out);
  or or_3 (ALUOp[0], and_6_out, and_7_out, and_8_out);
  and and_8 (and_8_out, opcode[3], opcode[0]);
  and and_9 (ALUSrc, not_1_out, opcode[2], not_3_out);
  and and_10 (Branch, not_4_out, not_3_out, not_2_out, not_1_out);
  and and_11 (and_11_out, opcode[1], not_4_out);
  or or_4 (RegWr, and_11_out, opcode[2], opcode[3]);
  and and_12 (MemtoReg, not_1_out, not_2_out, opcode[1], not_4_out);
  and and_13 (JumpImm, opcode[0], not_1_out, not_2_out, not_3_out);
  and and_14 (Incr, not_1_out, opcode[2], opcode[1], opcode[0]);
  and and_15 (MemWr, opcode[0], opcode[1], not_2_out, not_1_out);
endmodule

module pipeline1 (
  input  [7:0] PC,
  input  clk,
  input  [1:0] rb,
  input  [1:0] ra,
  input  reset,
  input  [3:0] imm,
  input  [3:0] opcode,
  input  [7:0] data,
  output [7:0] out_9,
  output [1:0] out_10,
  output [1:0] out_11,
  output [3:0] out_12,
  output [3:0] out_13,
  output [7:0] out_14
);

  Register register_1 (.D(PC), .en(1'b1), .clk(clk), .Q(out_9), .clr(reset));
  Register #(.width(2)) register_2 (.D(rb), .en(1'b1), .clk(clk), .Q(out_10), .clr(reset));
  Register #(.width(2)) register_3 (.D(ra), .en(1'b1), .clk(clk), .Q(out_11), .clr(reset));
  Register #(.width(4)) register_4 (.D(imm), .en(1'b1), .clk(clk), .Q(out_12), .clr(reset));
  Register #(.width(4)) register_5 (.D(opcode), .en(1'b1), .clk(clk), .Q(out_13), .clr(reset));
  Register register_6 (.D(data), .en(1'b1), .clk(clk), .Q(out_14), .clr(reset));
endmodule

module pipeline2 (
  input  MemtoReg,
  input  [7:0] data,
  input  [7:0] PC,
  input  clk,
  input  [7:0] rb,
  input  [7:0] ra,
  input  reset,
  input  [7:0] imm,
  input  [1:0] rd,
  input  [3:0] opcode,
  input  branch,
  input  incr,
  input  RegWr,
  input  [3:0] ALUOp,
  input  PCSrc,
  input  ALUSrc,
  input  MemWr,
  output out_18,
  output [7:0] out_19,
  output [7:0] out_20,
  output [7:0] out_21,
  output [7:0] out_22,
  output [7:0] out_23,
  output [1:0] out_24,
  output [3:0] out_25,
  output out_26,
  output out_27,
  output out_28,
  output [3:0] out_29,
  output out_30,
  output out_31,
  output out_32
);

  Register #(.width(1)) register_1 (.D(MemtoReg), .en(1'b1), .clk(clk), .Q(out_18), .clr(reset));
  Register register_2 (.D(data), .en(1'b1), .clk(clk), .Q(out_19), .clr(reset));
  Register register_3 (.D(PC), .en(1'b1), .clk(clk), .Q(out_20), .clr(reset));
  Register register_4 (.D(rb), .en(1'b1), .clk(clk), .Q(out_21), .clr(reset));
  Register register_5 (.D(ra), .en(1'b1), .clk(clk), .Q(out_22), .clr(reset));
  Register register_6 (.D(imm), .en(1'b1), .clk(clk), .Q(out_23), .clr(reset));
  Register #(.width(2)) register_7 (.D(rd), .en(1'b1), .clk(clk), .Q(out_24), .clr(reset));
  Register #(.width(4)) register_8 (.D(opcode), .en(1'b1), .clk(clk), .Q(out_25), .clr(reset));
  Register #(.width(1)) register_9 (.D(branch), .en(1'b1), .clk(clk), .Q(out_26), .clr(reset));
  Register #(.width(1)) register_10 (.D(incr), .en(1'b1), .clk(clk), .Q(out_27), .clr(reset));
  Register #(.width(1)) register_11 (.D(RegWr), .en(1'b1), .clk(clk), .Q(out_28), .clr(reset));
  Register #(.width(4)) register_12 (.D(ALUOp), .en(1'b1), .clk(clk), .Q(out_29), .clr(reset));
  Register #(.width(1)) register_13 (.D(PCSrc), .en(1'b1), .clk(clk), .Q(out_30), .clr(reset));
  Register #(.width(1)) register_14 (.D(ALUSrc), .en(1'b1), .clk(clk), .Q(out_31), .clr(reset));
  Register #(.width(1)) register_15 (.D(MemWr), .en(1'b1), .clk(clk), .Q(out_32), .clr(reset));
endmodule

module pipeline3 (
  input  branch,
  input  [7:0] PC,
  input  clk,
  input  [7:0] TA,
  input  [7:0] rULA,
  input  reset,
  input  [7:0] ra,
  input  [7:0] rb,
  input  [1:0] rd,
  input  zero,
  input  JumpImm,
  input  MemtoReg,
  input  ALUSrc,
  input  MemWr,
  output out_15,
  output [7:0] out_16,
  output [7:0] out_17,
  output [7:0] out_18,
  output [7:0] out_19,
  output [7:0] out_20,
  output [1:0] out_21,
  output out_22,
  output out_23,
  output out_24,
  output out_25,
  output out_26
);

  Register #(.width(1)) register_1 (.D(branch), .en(1'b1), .clk(clk), .Q(out_15));  // open: clr
  Register register_2 (.D(PC), .en(1'b1), .clk(clk), .Q(out_16));  // open: clr
  Register register_3 (.D(TA), .en(1'b1), .clk(clk), .Q(out_17));  // open: clr
  Register register_4 (.D(rULA), .en(1'b1), .clk(clk), .Q(out_18), .clr(reset));
  Register register_5 (.D(ra), .en(1'b1), .clk(clk), .Q(out_19), .clr(reset));
  Register register_6 (.D(rb), .en(1'b1), .clk(clk), .Q(out_20), .clr(reset));
  Register #(.width(2)) register_7 (.D(rd), .en(1'b1), .clk(clk), .Q(out_21), .clr(reset));
  Register #(.width(1)) register_8 (.D(zero), .en(1'b1), .clk(clk), .Q(out_22));  // open: clr
  Register #(.width(1)) register_9 (.D(JumpImm), .en(1'b1), .clk(clk), .Q(out_23));  // open: clr
  Register #(.width(1)) register_10 (.D(MemtoReg), .en(1'b1), .clk(clk), .Q(out_24), .clr(reset));
  Register #(.width(1)) register_11 (.D(ALUSrc), .en(1'b1), .clk(clk), .Q(out_25), .clr(reset));
  Register #(.width(1)) register_12 (.D(MemWr), .en(1'b1), .clk(clk), .Q(out_26), .clr(reset));
endmodule

module pipeline4 (
  input  [7:0] rULA,
  input  [7:0] mem,
  input  clk,
  input  [1:0] rd,
  input  reset,
  input  [3:0] opcode,
  input  [7:0] data,
  input  RegWr,
  input  MemtoReg,
  output [7:0] out_10,
  output [7:0] out_11,
  output [1:0] out_12,
  output [3:0] out_13,
  output [7:0] out_14,
  output out_15,
  output out_16
);

  Register register_1 (.D(rULA), .en(1'b1), .clk(clk), .Q(out_10), .clr(reset));
  Register register_2 (.D(mem), .en(1'b1), .clk(clk), .Q(out_11), .clr(reset));
  Register #(.width(2)) register_3 (.D(rd), .en(1'b1), .clk(clk), .Q(out_12), .clr(reset));
  Register #(.width(4)) register_4 (.D(opcode), .en(1'b1), .clk(clk), .Q(out_13), .clr(reset));
  Register register_5 (.D(data), .en(1'b1), .clk(clk), .Q(out_14), .clr(reset));
  Register #(.width(1)) register_6 (.D(RegWr), .en(1'b1), .clk(clk), .Q(out_15), .clr(reset));
  Register #(.width(1)) register_7 (.D(MemtoReg), .en(1'b1), .clk(clk), .Q(out_16), .clr(reset));
endmodule
